# Fritzing sketch schema (saved by Fritzing 0.9.3b)
breadboards: 1

parts:
  S1 = Pushbutton [package="[THT]"]
  S2 = Pushbutton [package="[THT]"]
  S3 = Pushbutton [package="[THT]"]
  Arduino_UNO = Arduino Uno (Rev3)
  M1 = DC Motor  # not connected
  LED1 = LED - 5mm [color="Red (633nm)" package="5 mm [THT]"]
  LED2 = LED - 5mm [color="Red (633nm)" package="5 mm [THT]"]
  LED3 = LED - 5mm [color="Red (633nm)" package="5 mm [THT]"]
  S4 = Pushbutton [package="[THT]"]
  S5 = Pushbutton [package="[THT]"]
  S6 = Pushbutton [package="[THT]"]
  LED4 = LED - 5mm [color="Red (633nm)" package="5 mm [THT]"]
  LED5 = LED - 5mm [color="Red (633nm)" package="5 mm [THT]"]
  LED6 = LED - 5mm [color="Red (633nm)" package="5 mm [THT]"]
  R1 = Resistor [tolerance=±5% resistance=220 package=THT]
  R2 = Resistor [tolerance=±5% resistance=220 package=THT]
  R3 = Resistor [tolerance=±5% resistance=220 package=THT]
  R4 = Resistor [tolerance=±5% resistance=220 package=THT]
  R5 = Resistor [tolerance=±5% resistance=220 package=THT]
  R6 = Resistor [tolerance=±5% resistance=220 package=THT]

nets:
  N1: S1.Pin_1, S1.Pin_2, S2.Pin_1, S2.Pin_2, S3.Pin_1, S3.Pin_2, Arduino_UNO.GND, S4.Pin_1, S4.Pin_2, S5.Pin_1, S5.Pin_2, S6.Pin_1, S6.Pin_2, R1.Pin_1, R2.Pin_1, R3.Pin_1, R4.Pin_1, R5.Pin_1, R6.Pin_1
  N2: S1.Pin_3, S1.Pin_4, Arduino_UNO.D1/TX
  N3: S2.Pin_3, S2.Pin_4, Arduino_UNO.D0/RX
  N4: S3.Pin_3, S3.Pin_4, Arduino_UNO.D2
  N5: Arduino_UNO.D8, LED6.cathode, R4.Pin_0
  N6: Arduino_UNO.D9_PWM, LED3.cathode, R1.Pin_0
  N7: Arduino_UNO.D10_PWM/SS, LED2.cathode, R2.Pin_0
  N8: Arduino_UNO.D11_PWM/MOSI, LED1.cathode, R3.Pin_0
  N9: Arduino_UNO.D3_PWM, S6.Pin_3, S6.Pin_4
  N10: Arduino_UNO.D4, S5.Pin_3, S5.Pin_4
  N11: Arduino_UNO.D5_PWM, S4.Pin_3, S4.Pin_4
  N12: Arduino_UNO.D6_PWM, LED4.anode
  N13: Arduino_UNO.D7, LED5.cathode, R5.Pin_0
  N14: LED4.cathode, R6.Pin_0
